# Fritzing sketch CircuitDiagram (saved by Fritzing 0.9.3b)

parts:
  Q1 = Basic FET N-Channel [package="DPak [SMD]"]
  D1 = Schottky Diode [part_number=1N5817 package="Melf DO-213 AB [SMD]"]
  D2 = Schottky Diode [part_number="Protects against reverse polarity battery by blowing fuse" package="Melf DO-213 AB [SMD]"]
  V1 = DC Power [voltage=5 part_number="Solar Array"]
  C1 = Electrolytic Capacitor [capacitance=47µF voltage=35V package="100 mil [THT, electrolytic]"]
  C2 = Electrolytic Capacitor [capacitance=10µF package="100 mil [THT, electrolytic]"]
  L1 = Inductor [inductance=100µH current=3.55A package="400 mil [THT]"]
  R1 = Resistor [tolerance=±5% resistance=15k package=THT]
  R2 = Resistor [tolerance=±5% resistance=220 package=THT]
  R3 = Resistor [tolerance=±5% resistance=22k package=THT]
  R4 = Resistor [tolerance=±5% resistance=10k package=THT]
  LED1 = LED - 5mm [color="Red (633nm)" package="5 mm [THT]"]
  R5 = Resistor [tolerance=±5% resistance=470 package=THT]
  JP1 = Header 3 [part_number="Programming Header" package=screwterminal-3.5mm-3_lock.007s]
  C3 = Electrolytic Capacitor [capacitance=1µF package="100 mil [THT, electrolytic]"]
  R7 = Resistor [tolerance=±5% resistance=10k package=THT]
  D3 = Schottky Diode [part_number="Prevents battery discharge through trim pot" package="300 mil [THT]"]
  R8 = Trimmer Potentiometer [maximum_resistance=10kΩ package=THT]
  F2 = FUSE [part_number="5A in Tractor" package=fuse_5mm]
  F1 = FUSE [part_number="3A In MPPT Box" package=fuse_5mm]
  BAT1 = FKIT-COIN_CELL [part_number="Tractor Battery" package=fkit-lir2450-h]
  C4 = Electrolytic Capacitor [capacitance=0.47mF voltage=35V package="100 mil [THT, electrolytic]"]
  C5 = Ceramic Capacitor [capacitance=100nF package="100 mil [THT, multilayer]"]
  J4 = Screw terminal - 2 pins [package=THT]
  J1 = Screw terminal - 2 pins [part_number="From Solar Array" package=THT]
  J3 = Screw terminal - 2 pins [package=THT]
  J2 = Screw terminal - 2 pins [part_number="To Battery" package=THT]
  IC2 = LP2950ACN-5.0 [package=to-92]
  IC1 = PICAXE-08M [package=THT]
  R6 = Resistor [tolerance=±5% resistance=10k package=THT]

nets:
  N1: Q1.Gate, IC1.In/Out_2_/_ADC_2_/_PWM_2, R6.Pin_1
  N2: Q1.drain, D1.anode, L1.pin_1
  GND: Q1.source, D2.anode, C1.-, C2.-, R2.Pin_0, R4.Pin_0, R5.Pin_0, JP1.1, C3.-, R8.leg1, C4.-, C5.0, J4.pin2, J3.pin2, IC2.GND, IC1.0V, R6.Pin_0
  N3: D1.cathode, D2.cathode, R7.Pin_1, D3.anode, C4.+
  N4: V1.V+, J1.pin1
  N5: V1.V-, J1.pin2
  N6: C1.+, L1.pin_0, R1.Pin_1, J4.pin1, IC2.IN
  5V: C2.+, C5.1, IC2.OUT, IC1.+V
  N7: R1.Pin_0, R2.Pin_1, C3.+, IC1.In/Out_4_/_ADC_4
  N8: R3.Pin_0, R4.Pin_1, IC1.Serial_In
  N9: R3.Pin_1, JP1.2
  N10: LED1.cathode, R5.Pin_1
  N11: LED1.anode, JP1.3, IC1.Serial_Out_/_Out_0_/_Infraout
  N12: R7.Pin_0, R8.leg2
  N13: D3.cathode, F1.1
  N14: R8.wiper, IC1.In/Out_1_/_ADC_1
  N15: F2.1, J2.pin1
  N16: F2.2, BAT1.POS
  N17: F1.2, J3.pin1
  N18: BAT1.NEG, J2.pin2

notes:
  D1 and D2 are in the same package

custom parts:
  LP2950ACN-5.0: LP2950ACN-5.0 3 Pin Low Dropout Linear Voltage Regulator
